// Logisim project 2021183642_Fahim Muntashir.circ as structural Verilog
module _7432_OR_gate (
  input  VCC,
  input  in_2,
  input  in_3,
  input  in_4,
  input  in_5,
  input  in_6,
  input  in_7,
  input  in_8,
  input  in_9,
  input  GND,
  output out_11,
  output out_12,
  output out_13,
  output out_14
);

  or or_1 (out_11, in_2, in_3);
  or or_2 (out_12, in_4, in_5);
  or or_3 (out_13, in_6, in_7);
  or or_4 (out_14, in_8, in_9);
endmodule

module _7402_NOR_gate (
  input  Vcc,
  input  in_2,
  input  in_3,
  input  in_4,
  input  in_5,
  input  in_6,
  input  in_7,
  input  in_8,
  input  in_9,
  input  GND,
  output out_11,
  output out_12,
  output out_13,
  output out_14
);

  nor nor_1 (out_11, in_2, in_3);
  nor nor_2 (out_12, in_4, in_5);
  nor nor_3 (out_13, in_6, in_7);
  nor nor_4 (out_14, in_8, in_9);
endmodule

module _7408_AND_gate (
  input  Vcc,
  input  in_2,
  input  in_3,
  input  in_4,
  input  in_5,
  input  in_6,
  input  in_7,
  input  in_8,
  input  in_9,
  input  GND,
  output out_11,
  output out_12,
  output out_13,
  output out_14
);

  and and_1 (out_11, in_2, in_3);
  and and_2 (out_12, in_4, in_5);
  and and_3 (out_13, in_6, in_7);
  and and_4 (out_14, in_8, in_9);
endmodule

module _7400_NAND_gate (
  input  Vcc,
  input  in_2,
  input  in_3,
  input  in_4,
  input  in_5,
  input  in_6,
  input  in_7,
  input  in_8,
  input  in_9,
  input  GND,
  output out_11,
  output out_12,
  output out_13,
  output out_14
);

  nand nand_1 (out_11, in_2, in_3);
  nand nand_2 (out_12, in_4, in_5);
  nand nand_3 (out_13, in_6, in_7);
  nand nand_4 (out_14, in_8, in_9);
endmodule

module _7486_XOR_gate (
  input  Vcc,
  input  in_2,
  input  in_3,
  input  in_4,
  input  in_5,
  input  in_6,
  input  in_7,
  input  in_8,
  input  in_9,
  input  GND,
  output out_11,
  output out_12,
  output out_13,
  output out_14
);

  xor xor_1 (out_11, in_2, in_3);
  xor xor_2 (out_12, in_4, in_5);
  xor xor_3 (out_13, in_6, in_7);
  xor xor_4 (out_14, in_8, in_9);
endmodule

module _7404_NOT_gate (
  input  Vcc,
  input  in_2,
  input  in_3,
  input  in_4,
  input  in_5,
  input  in_6,
  input  in_7,
  input  GND,
  output out_9,
  output out_10,
  output out_11,
  output out_12,
  output out_13,
  output out_14
);

  not not_1 (out_9, in_2);
  not not_2 (out_10, in_3);
  not not_3 (out_11, in_4);
  not not_4 (out_12, in_5);
  not not_5 (out_13, in_6);
  not not_6 (out_14, in_7);
endmodule
