// Logisim project 2021183642_Fahim Muntashir.circ as structural Verilog: 1 circuit, main circuit main
module main (
  input  A,
  input  B,
  input  C,
  output out_4,
  output p1_Output,
  output p2_Output
);

  wire and_1_out, and_2_out, nand_1_out, nand_2_out, nand_3_out, nand_4_out, nand_5_out, nand_6_out,
       nand_7_out, nand_8_out, nand_10_out, nand_11_out, not_1_out;

  not not_1 (not_1_out, C);
  nand nand_1 (nand_1_out, A, C);
  nand nand_2 (nand_2_out, C, C);
  nand nand_3 (nand_3_out, C, C);
  nand nand_4 (nand_4_out, B, nand_2_out);
  nand nand_5 (nand_5_out, A, C);
  nand nand_6 (nand_6_out, B, nand_3_out);
  and and_1 (and_1_out, A, C);
  and and_2 (and_2_out, B, not_1_out);
  nand nand_7 (nand_7_out, nand_1_out, nand_1_out);
  nand nand_8 (nand_8_out, nand_4_out, nand_4_out);
  or or_1 (out_4, and_1_out, and_2_out);
  nand nand_9 (p2_Output, nand_5_out, nand_6_out);
  nand nand_10 (nand_10_out, nand_7_out, nand_7_out);
  nand nand_11 (nand_11_out, nand_8_out, nand_8_out);
  nand nand_12 (p1_Output, nand_10_out, nand_11_out);
endmodule
